# Fritzing sketch design (saved by Fritzing 1.0.4)
circuit board: 8.83213cm x 5.43196cm
breadboards: 1

parts:
  R1 = Resistor [tolerance=±5% power=0.25W resistance=10k package=THT]
  Part1 = Arduino Uno (Rev3)
  NTC1 = Temperature Sensor (Thermistor) [thermistor_type=NTC package=THT]
  R3 = Resistor [tolerance=±5% power=0.25W resistance=10k package=THT]
  V1 = DC Power Supply [voltage=12V internal_resistance=0.1Ω max_current=10A]
  J_Fan1 = female pin header, 4 pins [form="♀ (female)"]
  J_uno_pins = female pin header, 5 pins [form="♀ (female)"]
  J_12v_supply = female pin header, 2 pins [form="♀ (female)"]
  J_NTC1 = female pin header, 2 pins [form="♀ (female)"]
  J_Fan2 = female pin header, 4 pins [form="♀ (female)"]

nets:
  N1: R1.Pin_0, Part1.GND, V1.Pin_1, J_Fan1.pin1, J_uno_pins.pin1, J_12v_supply.pin1, J_Fan2.pin1
  N2: R1.Pin_1, Part1.A2, NTC1.pin_0, J_uno_pins.pin3, J_NTC1.pin1
  N3: Part1.D3_PWM, R3.Pin_0, J_Fan1.pin3, J_uno_pins.pin5
  N4: Part1.D5_PWM, J_Fan1.pin4, J_uno_pins.pin4
  N5: Part1.5V, NTC1.pin_1, R3.Pin_1, J_uno_pins.pin2, J_NTC1.pin2
  N6: J_Fan1.pin2, J_12v_supply.pin2, J_Fan2.pin2
